// Logisim project cpu.circ as structural Verilog: 1 circuit, main circuit main
module main (
);

  wire and_1_out, and_2_out, and_3_out, and_4_out, and_5_out, and_6_out, button_1_out, button_2_out,
       button_3_out, button_4_out, button_5_out, clock_1_out, comparator_1_eq, comparator_2_eq,
       comparator_3_eq, comparator_4_eq, comparator_5_eq, d_ff_1_q, d_ff_1_qn, nor_1_out, nor_2_out,
       not_1_out, or_1_out, or_2_out, or_3_out, or_4_out;
  wire [6:0] controlled_buffer_3_out_2;
  wire [7:0] adder_2_out, negator_1_out, register_2_q, register_3_q, register_4_q, rom_1_data, rom_2_data;
  wire [15:0] adder_1_out, controlled_buffer_1_out, register_1_q;
  wire [15:7] controlled_buffer_3_out;

  Button button_1 (.out(button_1_out));
  Clock clock_1 (.out(clock_1_out));
  Button button_2 (.out(button_2_out));
  Register #(.width(16)) register_1 (
    .D(controlled_buffer_1_out), .Q(register_1_q), .clk(or_1_out), .clr(button_3_out));  // open: en
  D_Flip_Flop d_ff_1 (.clk(button_2_out), .D(d_ff_1_qn), .Q(d_ff_1_q), .Qn(d_ff_1_qn));  // open: preset, en, reset
  or or_1 (or_1_out, button_1_out, and_1_out);
  and and_1 (and_1_out, clock_1_out, d_ff_1_q);
  assign controlled_buffer_1_out = and_6_out ? {controlled_buffer_3_out, controlled_buffer_3_out_2} : 16'bz;  // Controlled_Buffer controlled_buffer_1
  assign controlled_buffer_1_out = not_1_out ? adder_1_out : 16'bz;  // Controlled_Buffer controlled_buffer_2
  Adder #(.width(16)) adder_1 (.a(register_1_q), .b(16'h1), .out(adder_1_out));  // open: cin, cout
  Button button_3 (.out(button_3_out));
  ROM #(.addrWidth(16)) rom_1 (.addr(register_1_q), .data(rom_1_data));  // open: sel
  ROM #(.addrWidth(16)) rom_2 (.addr(register_1_q), .data(rom_2_data));  // open: sel
  assign {controlled_buffer_3_out[7], controlled_buffer_3_out_2} = nor_1_out ? rom_2_data : 8'bz;  // Controlled_Buffer controlled_buffer_3
  nor nor_1 (nor_1_out, rom_1_data[4], rom_1_data[5], rom_1_data[6], rom_1_data[7]);
  not not_1 (not_1_out, and_6_out);
  Adder adder_2 (.a(register_4_q), .b(register_3_q), .out(adder_2_out));  // open: cin, cout
  Negator negator_1 (.in(register_3_q), .out(negator_1_out));
  Register register_2 (
    .D({controlled_buffer_3_out[7], controlled_buffer_3_out_2}), .en(rom_1_data[1]), .Q(register_2_q),
    .clk(or_1_out));  // open: clr
  Register register_3 (
    .D({controlled_buffer_3_out[7], controlled_buffer_3_out_2}), .en(rom_1_data[2]), .Q(register_3_q),
    .clk(or_1_out));  // open: clr
  Register register_4 (
    .D({controlled_buffer_3_out[7], controlled_buffer_3_out_2}), .en(rom_1_data[3]), .Q(register_4_q),
    .clk(or_1_out));  // open: clr
  assign {controlled_buffer_3_out[7], controlled_buffer_3_out_2} = rom_1_data[6] ? adder_2_out : 8'bz;  // Controlled_Buffer controlled_buffer_4
  assign {controlled_buffer_3_out[7], controlled_buffer_3_out_2} = rom_1_data[7] ? negator_1_out : 8'bz;  // Controlled_Buffer controlled_buffer_5
  Comparator #(.mode("unsigned")) comparator_1 (.a(register_2_q), .b(8'h1), .eq(comparator_1_eq));  // open: gt, lt
  Comparator #(.mode("unsigned")) comparator_2 (.a(register_2_q), .b(8'h2), .eq(comparator_2_eq));  // open: gt, lt
  Comparator #(.mode("unsigned")) comparator_3 (.a(register_2_q), .b(8'h3), .eq(comparator_3_eq));  // open: gt, lt
  Comparator #(.mode("unsigned")) comparator_4 (.a(register_2_q), .b(8'h4), .eq(comparator_4_eq));  // open: gt, lt
  Comparator #(.mode("unsigned")) comparator_5 (.a(register_2_q), .b(8'h7), .eq(comparator_5_eq));  // open: gt, lt
  RAM ram_1 (
    .addr(register_2_q), .data({controlled_buffer_3_out[7], controlled_buffer_3_out_2}), .sel(and_5_out),
    .clk(or_1_out), .ld(rom_1_data[4]), .clr(button_4_out));
  Button button_4 (.out(button_4_out));
  and and_2 (and_2_out, comparator_3_eq, register_3_q[7]);
  and and_3 (and_3_out, comparator_4_eq, register_3_q[7]);
  nor nor_2 (nor_2_out, comparator_1_eq, comparator_2_eq, comparator_3_eq, comparator_4_eq, comparator_5_eq);
  Register register_5 (
    .D({controlled_buffer_3_out[7], controlled_buffer_3_out_2}), .en(and_4_out),
    .Q(controlled_buffer_3_out[15:8]), .clk(or_1_out));  // open: clr
  and and_4 (and_4_out, rom_1_data[0], or_2_out);
  or or_2 (or_2_out, comparator_1_eq, and_2_out);
  or or_3 (or_3_out, comparator_2_eq, and_3_out);
  or or_4 (or_4_out, rom_1_data[0], rom_1_data[4]);
  and and_5 (and_5_out, or_4_out, nor_2_out);
  and and_6 (and_6_out, rom_1_data[0], or_3_out);
  TTY #(.rows(35), .cols(120)) tty_1 (
    .data(controlled_buffer_3_out_2), .clk(or_1_out), .we(comparator_5_eq), .clr(button_5_out));
  Button button_5 (.out(button_5_out));

  // Notes on the sheet:
  //   Clock step
  //   Clock en
  //   Reset
  //   contents of rom_1 (hex, n*v repeats v):
  //   2 1 2 1 0 2 14 8 2 41 2 1 2 18 2 14 84 44 8 2 1 2 1 84 2 1 2 1 2 1 2 1 2 1 0 2 1 0 2 14 8 44 2 1 2 1
  //   2 1 2 1 2 1 0 2 14 8 2 41 2 14 8 2 41 2 1 2 18 2 14 84 44 8 2 1 2 1 2 1 2 1 2 1 0 2 1 0 2 14 8 44 2
  //   1 2 1 2 1 2 1 2 14 8 2 41 2 18 2 14 84 2 41 0 2 1 2 14 8 2 41 0 2 14 8 2 41 2 1 2 18 2 14 84 44 8 84
  //   2 1 2 1 2 1 2 1 2 1 0 2 1 0 2 14 8 44 2 1 2 1 2 14 8 2 41 2 1 2 18 2 14 2 41 2 14 8 2 41 2 1 2 14 8
  //   2 41 2 1 0 2 14 2 1 2 1 2 14 8 41 2 14 84 2 18 41 2 1 2 1 0 2 1 2 1 0 2 14 8 2 41 2 1 2 18 2 14 84 2
  //   41 0 2 14 8 2 41 2 1 2 18 2 14 84 44 8 84 8 44 2 1 2 1 2 1 2 1 2 1 0 2 1 0 2 14 8 44 2 1 2 1 2 14 8
  //   2 41 2 1 0 2 14 8 2 41 2 14 8 2 41 2 18 2 14 84 44 8 2 1 2 1 2 1 2 1 2 1 0 2 1 0 2 14 8 44 2 1 2 1 2
  //   14 8 2 41 2 1 2 14 8 2 41 2 1 0 2 14 2 1 2 1 2 14 8 41 2 14 84 2 18 41 2 1 2 1 0 2 14 8 2 41 2 1 2
  //   18 2 14 2 41 2 1 2 1 0 2 1 2 14 8 2 41 2 1 0 2 14 2 1 2 1 2 14 84 2 18 41 2 1 2 1 0 2 14 2 18 41 2
  //   18 2 14 2 41 2 14 8 2 41 2 1 2 18 2 14 84 2 41 2 1 2 1 0 0 2 14 8 2 41 2 14 2 41 0 2 1 2 1 0 2 14 8
  //   2 41 2 1 2 18 2 14 84 44 8 2 1 2 1 2 1 2 1 2 1 0 2 1 0 2 14 8 44 2 1 2 1 2 1 0 2 14 8 2 41 2 1 2 18
  //   2 14 84 44 8 2 1 2 1 2 1 2 1 2 1 0 2 1 0 2 14 8 44 2 1 2 1 2 14 8 2 41 2 1 2 14 8 2 41 2 1 0 2 14 2
  //   1 2 1 2 14 8 41 2 14 84 2 18 41 2 1 2 1 0 2 14 8 2 41 2 14 8 2 41 2 1 0 2 14 2 1 2 1 2 14 84 2 18 41
  //   2 1 2 1 0 2 14 2 18 41 2 1 2 18 2 14 84 44 8 2 1 2 1 84 2 1 2 1 2 1 2 1 2 1 0 2 1 0 2 14 8 44 2 1 2
  //   1 2 14 8 2 41 2 1 2 18 2 14 84 2 41 0 2 14 8 2 41 2 14 8 2 41 2 14 8 2 41 2 14 8 2 41 2 1 0 2 14 2 1
  //   2 1 2 18 2 14 41 2 14 8 41 2 1 2 1 0 2 14 8 2 41 2 18 2 14 2 41 2 14 8 2 41 2 14 8 2 41 2 14 8 2 41
  //   2 14 8 2 41 2 1 0 2 14 2 1 2 1 2 18 2 14 41 2 14 8 41 2 1 2 1 0 2 14 8 2 41 2 18 2 14 2 41 2 1 2 14
  //   8 2 41 2 18 2 14 84 2 41 2 14 8 2 41 2 14 8 2 41 2 18 2 14 84 44 8 2 1 2 1 84 2 1 2 1 2 1 2 1 2 1 0
  //   2 1 0 2 1 2 14 8 2 41 2 1 0 2 14 2 1 2 1 2 14 84 2 18 41 2 1 2 1 0 2 14 2 18 41 2 1 2 18 2 14 84 44
  //   8 2 1 2 1 84 2 1 2 1 2 1 2 1 2 1 0 2 1 0 2 14 8 44 2 1 2 1 2 14 8 2 41 2 14 8 2 41 2 18 2 14 84 44 8
  //   84 8 44 2 1 2 1 2 1 2 1 2 1 0 2 1 0 2 14 8 2 41 2 14 8 2 41 2 18 2 14 84 44 8 84 2 1 2 1 2 1 2 1 2 1
  //   0 2 1 0 2 14 8 44 2 1 2 1 2 1 0 0 2 14 8 2 41 2 14 8 44 2 1 2 1 2 14 8 2 41 2 1 0 2 14 2 1 2 1 2 14
  //   84 2 18 41 2 1 2 1 0 2 14 2 18 41 2 1 2 18 2 14 84 44 8 2 1 2 1 84 2 1 2 1 2 1 2 1 2 1 0 2 1 0 2 14
  //   8 44 2 1 2 1 2 14 8 2 41 2 1 2 1 2 1 2 1 0 2 14 8 2 41 2 1 2 18 2 14 84 44 8 2 1 2 1 2 1 2 1 2 1 0 2
  //   1 0 2 14 8 44 2 1 2 1 2 1 0 2 1 2 1 0 2 1 1 0 2 1 2 1 0 2 14 8 2 41 2 14 8 44 2 1 2 1 2 1 1 2 1 2 1
  //   0 2 1 1 0 0 2 14 8 2 41 2 1 2 18 2 14 2 41 2 1 2 1 0 2 1 2 14 8 2 41 2 1 2 18 2 14 2 41 2 1 2 1 0 0
  //   2 1 2 1
  //   contents of rom_2 (hex, n*v repeats v):
  //   1 1 2 b0 0 e 0 0 8 0 9 0 8 0 9 4*0 3 0 4 22 0 3 0 4 22 8 1 1 0 2 25 0 8 0 0 8 0 ff 0 3 0 4 34 7 30 1
  //   1 2 a6 0 e 0 0 f 0 f 0 0 8 0 9 0 8 0 9 4*0 3 0 4 52 8 0 1 0 2 55 0 8 1 0 8 0 ff 0 3 0 4 6e 7 2d 8 0
  //   e 0 0 9 0 8 0 9 0 0 f 0 0 11 0 f 0 0 10 0 0 10 0 0 8 0 9 0 8 0 9 5*0 3 0 4 90 8 0 1 0 2 93 0 8 1 0 8
  //   0 ff 0 3 0 4 d1 11 0 0 8 0 9 1 8 0 9 0 11 0 10 0 0 8 0 9 a 8 0 0 d 0 10 ff 0 d 0 3 0 4 cc 10 0 1 0 9
  //   0 0 d 0 0 1 0 2 b7 0 1 0 2 76 0 11 0 0 8 0 9 1 8 0 9 0 0 12 0 0 12 0 0 8 0 9 0 8 0 9 5*0 ff 0 3 0 4
  //   fc 8 0 1 0 2 ff 0 8 1 0 8 0 ff 0 3 1 4 a5 f 0 0 14 0 13 0 0 13 0 0 8 0 12 0 0 9 0 8 0 9 4*0 3 1 4 2b
  //   8 0 1 1 2 2e 0 8 1 0 8 0 ff 0 3 1 4 6c 14 0 0 8 0 9 a 8 0 0 d 0 14 ff 0 d 0 3 1 4 5a 14 0 1 0 9 0 0
  //   d 0 0 1 1 2 45 0 13 0 0 8 0 9 1 8 0 9 0 13 0 1 1 2 f 0 8 30 14 0 0 9 0 a a 0 9 0 3 1 4 87 a 0 0 9 0
  //   0 1 1 2 76 0 a 0 9 0 0 8 0 9 0 7 0 12 0 0 8 0 9 1 8 0 9 0 0 12 0 1 0 2 e0 0 0 5 0 0 1 0 6 0 2 0 0 15
  //   0 16 8 0 16 0 0 8 0 9 1b 8 0 9 4*0 3 1 4 ce 8 0 1 1 2 d1 0 8 1 0 8 0 ff 0 3 4 4 7c 17 0 0 17 0 0 8 0
  //   9 3c 8 0 9 4*0 3 1 4 f5 8 0 1 1 2 f8 0 8 1 0 8 0 ff 0 3 4 4 68 17 0 0 8 0 9 a 8 0 0 d 0 18 ff 0 d 0
  //   3 2 4 24 18 0 1 0 9 0 0 d 0 0 1 2 2 f 0 18 0 0 19 0 17 0 0 8 0 9 5 0 8 0 3 2 4 42 9 0 0 8 0 0 1 2 2
  //   31 0 9 0 8 0 0 9 0 8 0 9 4*0 3 2 4 60 0 3 2 4 60 8 1 1 2 2 63 0 8 0 0 8 0 ff 0 3 2 4 7a 19 0 0 8 0 9
  //   1 8 0 9 0 0 19 0 0 18 0 0 8 0 18 0 0 9 0 9 0 ff d 0 8 0 0 9 0 8 0 0 d 0 3 2 4 a5 9 0 8 0 0 d 0 ff 0
  //   1 2 2 91 0 15 0 0 9 0 8 0 9 0 1a 0 19 0 0 8 0 19 0 0 9 0 9 0 ff d 0 8 0 0 9 0 8 0 0 d 0 3 2 4 db 9 0
  //   8 0 0 d 0 ff 0 1 2 2 c7 0 15 0 0 9 0 8 0 9 0 1b 0 8 19 16 0 0 9 0 8 0 9 0 0 1c 0 1a 0 0 8 0 1c 0 0 9
  //   0 8 0 9 4*0 3 3 4 15 0 3 3 4 15 1d 1 1 3 2 18 0 1d 0 0 1e 0 17 0 0 8 0 9 a 0 8 0 3 3 4 33 9 0 0 8 0
  //   0 1 3 2 22 0 9 0 8 0 0 9 0 8 0 9 4*0 3 3 4 51 0 3 3 4 51 8 1 1 3 2 54 0 8 0 0 8 0 ff 0 3 3 4 aa 1c 0
  //   0 8 0 1b 0 0 9 0 8 0 9 5*0 ff 0 3 3 4 7b 1e 0 1 3 2 7e 0 1e 1 0 1c 0 0 8 0 1a 0 0 9 0 8 0 9 5*0 3 3
  //   4 9b 8 0 1 3 2 9e 0 8 1 0 8 0 ff 0 3 3 4 a9 1e 0 0 0 1d 0 0 8 0 8 0 ff 0 3 4 4 3c 17 0 0 8 0 9 a 0 8
  //   0 3 3 4 d0 9 0 0 8 0 0 1 3 2 bf 0 9 0 8 0 0 9 0 8 0 9 4*0 3 3 4 ee 0 3 3 4 ee 8 1 1 3 2 f1 0 8 0 0 8
  //   0 ff 0 3 4 4 33 18 0 0 e 0 5 4 6 7 1 0 2 4 0 18 0 0 8 0 9 a 8 0 9 4*0 3 4 4 20 8 0 1 4 2 23 0 8 1 0
  //   8 0 ff 0 3 4 4 2e 7 5f 0 1 4 2 37 0 7 5f 5f 0 1 4 2 56 0 1e 0 0 8 0 8 0 ff 0 3 4 4 51 7 7c 20 1 4 2
  //   55 0 7 2e 20 0 0 17 0 0 8 0 9 1 8 0 9 0 17 0 1 1 2 dc 0 7 a 16 0 0 8 0 9 1 8 0 9 0 16 0 1 1 2 b5 0 0
  //   1 4 2 7d
  //   RAM Reset
  //   Clear
endmodule
